// Logisim project 1bitmemorycell.circ as structural Verilog
module main (
  input  WE,
  input  D,
  input  OE,
  input  RESET
);

  wire and_1_out, and_2_out, CLK_out, controlled_buffer_1_out, d_ff_1_q, d_ff_1_qn, not_1_out, or_1_out;

  Clock CLK (.out(CLK_out));
  not not_1 (not_1_out, WE);
  and and_1 (and_1_out, d_ff_1_q, not_1_out);
  and and_2 (and_2_out, WE, D);
  or or_1 (or_1_out, and_1_out, and_2_out);
  D_Flip_Flop d_ff_1 (.D(or_1_out), .clk(CLK_out), .Q(d_ff_1_q), .Qn(d_ff_1_qn), .reset(RESET));  // open: preset
  assign controlled_buffer_1_out = OE ? d_ff_1_q : 1'bz;  // Controlled_Buffer controlled_buffer_1

  // Notes on the sheet:
  //   temp_D
  //   QNOT
  //   DOUT
endmodule

// VHDL entity dff, as the project stores it:
library ieee;
use ieee.std_logic_1164.all;

entity dff is
  port (
    CLK   : in std_logic;
    D   : in std_logic;
    RESET : in std_logic;
    Q  : out std_logic;
    QNOT: out std_logic
  );
end dff;

architecture behv of dff is
begin

  process(CLK, RESET)
  begin
    if (RESET = '1') then
      Q <= '0';
      QNOT <= '1';
    elsif rising_edge(CLK) then
      Q <= D;
      QNOT <= not D;
    end if;
  end process;

end behv;

// VHDL entity tristate, as the project stores it:
library ieee;
use ieee.std_logic_1164.all;

entity tristate is
  port (
    A: in std_logic;
    EN: in std_logic;
    Y: out std_logic
  );
end tristate;

architecture arch of tristate is
begin
    tristate_process: process(A, EN)
    begin
        if (EN = '1') then
            Y <= A;
        else
            Y <= 'Z'; -- Use 'Z' for tristate
        end if;
    end process tristate_process;
end arch;

// VHDL entity memoryCell, as the project stores it:
library ieee;
use ieee.std_logic_1164.all;

entity memoryCell is
  port (
    CLK   : in std_logic;
    D   : in std_logic;
    RESET : in std_logic;
    WE: in std_logic; -- write enable
    OE: in std_logic; -- output enable
    Q  : out std_logic;
    QNOT: out std_logic;
    DOUT: out std_logic -- output of tristate buffer stage
  ) ;
end memoryCell;

architecture mem of memoryCell is

    signal temp_D: std_logic;
    begin
        temp_D <= ((not WE) and Q) or (WE and D);
        dff_inst: dff
        PORT(
            CLK  => CLK,
            D => temp_D,
            RESET => RESET,
            Q => Q,
            QNOT => QNOT
        );

        tri_inst: tristate
        PORT(
            A => Q, 
            EN => OE,
            Y => DOUT
        );
end mem;
